// Logisim project circuito.circ as structural Verilog: 10 circuits, main circuit main
module main (
  input  in_1,
  input  in_2,
  input  in_3,
  input  in_4,
  input  in_5,
  input  in_6,
  input  in_7,
  input  in_8,
  input  in_9,
  input  in_10,
  input  in_11,
  input  in_12,
  input  in_13,
  input  in_14,
  output A4,
  output A3,
  output A2,
  output A1,
  output B4,
  output B3,
  output B2,
  output B1
);

  _7_Segment_Display u_7_segment_display_1 (
    .g(in_4), .f(in_2), .a(in_1), .b(in_3), .e(in_5), .d(in_7), .c(in_6));  // open: dp
  _7_Segment_Display u_7_segment_display_2 (
    .g(in_11), .f(in_9), .a(in_8), .b(in_10), .e(in_12), .d(in_14), .c(in_13));  // open: dp
  conversor conversor_1 (
    .a(in_1), .b(in_3), .c(in_6), .d(in_7), .e(in_5), .f(in_2), .g(in_4), .X4(A4), .X3(A3), .X2(A2), .X1(A1));
  conversor conversor_2 (
    .a(in_8), .b(in_10), .c(in_13), .d(in_14), .e(in_12), .f(in_9), .g(in_11), .X4(B4), .X3(B3), .X2(B2),
    .X1(B1));
  calculador calculador_1 (
    .A1(A1), .A3(A2), .A2(A3), .A4(A4), .B1(B1), .B2(B2), .B3(B3), .B4(B4));  // open: out_14, out_13, out_12, out_11, ci, out_10
endmodule

module conversor (
  input  a,
  input  b,
  input  c,
  input  d,
  input  e,
  input  f,
  input  g,
  output X4,
  output X3,
  output X2,
  output X1
);

  wire and_1_out, and_2_out, and_3_out, and_4_out, and_5_out, and_6_out, and_7_out, and_8_out, and_9_out,
       and_10_out, and_11_out, and_12_out, and_13_out, and_14_out, and_15_out, and_16_out, and_17_out,
       and_18_out, and_19_out, and_20_out, and_21_out, and_22_out, and_23_out, not_1_out, not_2_out,
       not_3_out, not_4_out, not_5_out, not_6_out, not_7_out, not_8_out, not_9_out, not_10_out, not_11_out,
       not_12_out, not_13_out, not_14_out, not_15_out, not_16_out, not_17_out, not_18_out, not_19_out,
       not_20_out, not_21_out, not_22_out, not_23_out, not_24_out, not_25_out, not_26_out, not_27_out,
       not_28_out, not_29_out, not_30_out, not_31_out, not_32_out, not_33_out, not_34_out, not_35_out,
       not_36_out, not_37_out, not_38_out, not_39_out, not_40_out, not_41_out, not_42_out, not_43_out,
       not_44_out, not_45_out, not_46_out;

  not not_1 (not_1_out, a);
  not not_2 (not_2_out, b);
  not not_3 (not_3_out, f);
  not not_4 (not_4_out, b);
  not not_5 (not_5_out, c);
  not not_6 (not_6_out, b);
  not not_7 (not_7_out, c);
  not not_8 (not_8_out, a);
  not not_9 (not_9_out, d);
  not not_10 (not_10_out, e);
  not not_11 (not_11_out, a);
  not not_12 (not_12_out, f);
  not not_13 (not_13_out, b);
  not not_14 (not_14_out, c);
  not not_15 (not_15_out, b);
  not not_16 (not_16_out, c);
  not not_17 (not_17_out, b);
  not not_18 (not_18_out, d);
  not not_19 (not_19_out, e);
  not not_20 (not_20_out, f);
  not not_21 (not_21_out, g);
  not not_22 (not_22_out, b);
  not not_23 (not_23_out, b);
  not not_24 (not_24_out, c);
  not not_25 (not_25_out, c);
  not not_26 (not_26_out, f);
  not not_27 (not_27_out, d);
  not not_28 (not_28_out, e);
  not not_29 (not_29_out, f);
  not not_30 (not_30_out, g);
  not not_31 (not_31_out, d);
  not not_32 (not_32_out, e);
  not not_33 (not_33_out, f);
  not not_34 (not_34_out, a);
  not not_35 (not_35_out, b);
  not not_36 (not_36_out, d);
  not not_37 (not_37_out, e);
  not not_38 (not_38_out, f);
  not not_39 (not_39_out, g);
  not not_40 (not_40_out, f);
  not not_41 (not_41_out, b);
  not not_42 (not_42_out, c);
  not not_43 (not_43_out, d);
  not not_44 (not_44_out, b);
  not not_45 (not_45_out, e);
  not not_46 (not_46_out, f);
  and and_1 (and_1_out, not_1_out, not_2_out, c, d, e, f, g);
  and and_2 (and_2_out, b, c, d, e, not_3_out, g);
  and and_3 (and_3_out, a, not_4_out, not_5_out, e, f, g);
  and and_4 (and_4_out, a, not_6_out, not_7_out, d, e, f);
  and and_5 (and_5_out, a, b, c, e, f, g);
  and and_6 (and_6_out, not_8_out, b, c, not_9_out, not_10_out, f, g);
  and and_7 (and_7_out, not_11_out, b, c, d, e, not_12_out, g);
  and and_8 (and_8_out, a, not_13_out, not_14_out, e, f, g);
  and and_9 (and_9_out, a, not_15_out, not_16_out, d, e, f);
  and and_10 (and_10_out, a, not_17_out, c, d, f, g);
  and and_11 (and_11_out, a, b, c, not_18_out, not_19_out, not_20_out, not_21_out);
  and and_12 (and_12_out, not_22_out, c, d, e, f, g);
  and and_13 (and_13_out, a, not_23_out, not_24_out, e, f, g);
  and and_14 (and_14_out, a, b, not_25_out, d, e, not_26_out, g);
  and and_15 (and_15_out, a, b, c, not_27_out, not_28_out, not_29_out, not_30_out);
  and and_16 (and_16_out, a, b, c, not_31_out, e, f, g);
  and and_17 (and_17_out, a, b, c, d, not_32_out, not_33_out, g);
  and and_18 (and_18_out, not_34_out, not_35_out, c, d, e, f, g);
  and and_19 (and_19_out, b, c, not_36_out, not_37_out, not_38_out, not_39_out);
  and and_20 (and_20_out, b, c, d, e, not_40_out, g);
  and and_21 (and_21_out, a, not_41_out, not_42_out, not_43_out, e, f, g);
  and and_22 (and_22_out, a, not_44_out, c, d, not_45_out, f, g);
  and and_23 (and_23_out, a, b, c, d, not_46_out, g);
  or or_1 (X4, and_1_out, and_2_out, and_3_out, and_4_out, and_5_out);
  or or_2 (X3, and_6_out, and_7_out, and_8_out, and_9_out, and_10_out, and_11_out);
  or or_3 (X2, and_12_out, and_13_out, and_14_out, and_15_out, and_16_out, and_17_out);
  or or_4 (X1, and_18_out, and_19_out, and_20_out, and_21_out, and_22_out, and_23_out);
endmodule

module calculador (
  input  ci,
  input  A4,
  input  A3,
  input  A2,
  input  A1,
  input  B4,
  input  B3,
  input  B2,
  input  B1,
  output out_10,
  output out_11,
  output out_12,
  output out_13,
  output out_14
);

  somador somador_1 (
    .ci(ci), .a0(A1), .b0(B1), .a1(A2), .b1(B2), .a2(A3), .b2(B3), .a3(A4), .b3(B4), .s0(out_14),
    .s1(out_13), .s2(out_12), .s3(out_11), .co(out_10));
endmodule

module multiplexador (
  input  op1,
  input  op2,
  output soma,
  output subt,
  output mult,
  output divi
);

  wire not_1_out, not_2_out, not_3_out, not_4_out;

  not not_1 (not_1_out, op1);
  not not_2 (not_2_out, op2);
  not not_3 (not_3_out, op1);
  not not_4 (not_4_out, op2);
  and and_1 (divi, op1, op2);
  and and_2 (soma, not_1_out, not_2_out);
  and and_3 (subt, not_3_out, op2);
  and and_4 (mult, op1, not_4_out);
endmodule

module somador (
  input  ci,
  input  a0,
  input  b0,
  input  a1,
  input  b1,
  input  a2,
  input  b2,
  input  a3,
  input  b3,
  output s0,
  output s1,
  output s2,
  output s3,
  output co
);

  wire somador_inteiro_1_co, somador_inteiro_2_co, somador_inteiro_3_co;

  somador_inteiro somador_inteiro_1 (.ci(ci), .a(a0), .b(b0), .S(s0), .co(somador_inteiro_1_co));
  somador_inteiro somador_inteiro_2 (.ci(somador_inteiro_1_co), .a(a1), .b(b1), .S(s1), .co(somador_inteiro_2_co));
  somador_inteiro somador_inteiro_3 (.ci(somador_inteiro_2_co), .a(a2), .b(b2), .S(s2), .co(somador_inteiro_3_co));
  somador_inteiro somador_inteiro_4 (.ci(somador_inteiro_3_co), .a(a3), .b(b3), .S(s3), .co(co));
endmodule

module meio_somador (
  input  a,
  input  b,
  output S,
  output c0
);

  xor xor_1 (S, a, b);
  and and_1 (c0, a, b);
endmodule

module somador_inteiro (
  input  ci,
  input  a,
  input  b,
  output S,
  output co
);

  wire meio_somador_1_c0, meio_somador_1_s, meio_somador_2_c0;

  meio_somador meio_somador_1 (.a(a), .b(b), .S(meio_somador_1_s), .c0(meio_somador_1_c0));
  meio_somador meio_somador_2 (.a(ci), .b(meio_somador_1_s), .S(S), .c0(meio_somador_2_c0));
  or or_1 (co, meio_somador_2_c0, meio_somador_1_c0);
endmodule

module meio_subtrator (
  input  a,
  input  b,
  output S,
  output to
);

  wire not_1_out;

  xor xor_1 (S, a, b);
  not not_1 (not_1_out, a);
  and and_1 (to, not_1_out, b);
endmodule

module subtrator_inteiro (
  input  ti,
  input  a,
  input  b,
  output S,
  output to
);

  wire meio_subtrator_1_s, meio_subtrator_1_to, meio_subtrator_2_to;

  meio_subtrator meio_subtrator_1 (.a(a), .b(b), .S(meio_subtrator_1_s), .to(meio_subtrator_1_to));
  meio_subtrator meio_subtrator_2 (.a(ti), .b(meio_subtrator_1_s), .S(S), .to(meio_subtrator_2_to));
  and and_1 (to, meio_subtrator_2_to, meio_subtrator_1_to);
endmodule

module subtrator (
  input  in_1,
  input  in_2,
  input  in_3,
  input  in_4,
  input  in_5,
  input  in_6,
  input  in_7,
  input  in_8,
  input  in_9,
  output out_10,
  output out_11,
  output out_12,
  output out_13,
  output result
);

  wire subtrator_inteiro_1_to, subtrator_inteiro_2_to, subtrator_inteiro_3_to;

  subtrator_inteiro subtrator_inteiro_1 (.ti(in_1), .a(in_2), .b(in_3), .S(out_10), .to(subtrator_inteiro_1_to));
  subtrator_inteiro subtrator_inteiro_2 (
    .ti(subtrator_inteiro_1_to), .a(in_4), .b(in_5), .S(out_11), .to(subtrator_inteiro_2_to));
  subtrator_inteiro subtrator_inteiro_3 (
    .ti(subtrator_inteiro_2_to), .a(in_6), .b(in_7), .S(out_12), .to(subtrator_inteiro_3_to));
  subtrator_inteiro subtrator_inteiro_4 (.ti(subtrator_inteiro_3_to), .a(in_8), .b(in_9), .S(out_13), .to(result));
endmodule
